// Logisim project Второй видос.circ as structural Verilog
module \_8_битный_регистр  (
  input  in_1,
  input  [7:0] in_2,
  input  Enable,
  input  Clear,
  output [7:0] out_5
);

  D_Flip_Flop d_ff_1 (.clk(in_1), .D(in_2[0]), .Q(out_5[0]), .en(Enable), .reset(Clear));  // open: Qn, preset
  D_Flip_Flop d_ff_2 (.clk(in_1), .D(in_2[1]), .Q(out_5[1]), .en(Enable), .reset(Clear));  // open: Qn, preset
  D_Flip_Flop d_ff_3 (.clk(in_1), .D(in_2[2]), .Q(out_5[2]), .en(Enable), .reset(Clear));  // open: Qn, preset
  D_Flip_Flop d_ff_4 (.clk(in_1), .D(in_2[3]), .Q(out_5[3]), .en(Enable), .reset(Clear));  // open: Qn, preset
  D_Flip_Flop d_ff_5 (.clk(in_1), .D(in_2[4]), .Q(out_5[4]), .en(Enable), .reset(Clear));  // open: Qn, preset
  D_Flip_Flop #(.trigger("high")) d_ff_6 (
    .clk(in_1), .D(in_2[5]), .Q(out_5[5]), .en(Enable), .reset(Clear));  // open: Qn, preset
  D_Flip_Flop d_ff_7 (.clk(in_1), .D(in_2[6]), .Q(out_5[6]), .en(Enable), .reset(Clear));  // open: Qn, preset
  D_Flip_Flop d_ff_8 (.clk(in_1), .D(in_2[7]), .Q(out_5[7]), .en(Enable), .reset(Clear));  // open: Qn, preset
endmodule

module \_8_битный_сумматор  (
  input  in_1,
  input  [7:0] in_2,
  input  [7:0] in_3,
  output out_4,
  output [7:0] out_5
);

  wire \сумматор_1_перенос , \сумматор_2_перенос , \сумматор_3_перенос , \сумматор_4_перенос ,
       \сумматор_5_перенос , \сумматор_6_перенос , \сумматор_7_перенос ;
  wire [7:0] \инвертор_1_out_3 ;

  // Probe on in_3
  // Probe on out_5
  \Сумматор  \u_сумматор_1  (
    .\Сумма (out_5[0]), .\Перенос (\сумматор_1_перенос ), .A(in_3[0]), .B(\инвертор_1_out_3 [0]), .C(in_1));
  \Сумматор  \u_сумматор_2  (
    .\Сумма (out_5[1]), .\Перенос (\сумматор_2_перенос ), .A(in_3[1]), .B(\инвертор_1_out_3 [1]),
    .C(\сумматор_1_перенос ));
  // Probe on in_2
  \Сумматор  \u_сумматор_3  (
    .\Сумма (out_5[3]), .\Перенос (\сумматор_3_перенос ), .A(in_3[3]), .B(\инвертор_1_out_3 [3]),
    .C(\сумматор_4_перенос ));
  \Сумматор  \u_сумматор_4  (
    .\Сумма (out_5[2]), .\Перенос (\сумматор_4_перенос ), .A(in_3[2]), .B(\инвертор_1_out_3 [2]),
    .C(\сумматор_2_перенос ));
  \Сумматор  \u_сумматор_5  (
    .\Сумма (out_5[4]), .\Перенос (\сумматор_5_перенос ), .A(in_3[4]), .B(\инвертор_1_out_3 [4]),
    .C(\сумматор_3_перенос ));
  \Сумматор  \u_сумматор_6  (
    .\Сумма (out_5[5]), .\Перенос (\сумматор_6_перенос ), .A(in_3[5]), .B(\инвертор_1_out_3 [5]),
    .C(\сумматор_5_перенос ));
  \Сумматор  \u_сумматор_7  (
    .\Сумма (out_5[6]), .\Перенос (\сумматор_7_перенос ), .A(in_3[6]), .B(\инвертор_1_out_3 [6]),
    .C(\сумматор_6_перенос ));
  // Probe on \инвертор_1_out_3 
  \Сумматор  \u_сумматор_8  (
    .\Сумма (out_5[7]), .\Перенос (out_4), .A(in_3[7]), .B(\инвертор_1_out_3 [7]), .C(\сумматор_7_перенос ));
  \Инвертор  \u_инвертор_1  (.in_2(in_1), .out_3(\инвертор_1_out_3 ), .in_1(in_2));
endmodule

module \Полусумматор  (
  input  \А ,
  input  \В ,
  output \Сумма ,
  output \Перенос 
);

  xor xor_1 (\Сумма , \А , \В );
  and and_1 (\Перенос , \А , \В );
endmodule

module \Сумматор  (
  input  A,
  input  B,
  input  C,
  output \Сумма ,
  output \Перенос 
);

  wire \полусумматор_1_перенос , \полусумматор_1_сумма , \полусумматор_2_перенос ;

  \Полусумматор  \u_полусумматор_1  (
    .\Сумма (\полусумматор_1_сумма ), .\Перенос (\полусумматор_1_перенос ), .\А (A), .\В (B));
  \Полусумматор  \u_полусумматор_2  (
    .\Сумма (\Сумма ), .\Перенос (\полусумматор_2_перенос ), .\А (C), .\В (\полусумматор_1_сумма ));
  or or_1 (\Перенос , \полусумматор_2_перенос , \полусумматор_1_перенос );
endmodule

module \Инвертор  (
  input  [7:0] in_1,
  input  in_2,
  output [7:0] out_3
);

  // Probe on in_1
  // Probe on out_3
  xor xor_1 (out_3[7], in_2, in_1[7]);
  xor xor_2 (out_3[6], in_2, in_1[6]);
  xor xor_3 (out_3[5], in_2, in_1[5]);
  xor xor_4 (out_3[4], in_2, in_1[4]);
  xor xor_5 (out_3[3], in_2, in_1[3]);
  xor xor_6 (out_3[2], in_2, in_1[2]);
  xor xor_7 (out_3[1], in_2, in_1[1]);
  xor xor_8 (out_3[0], in_2, in_1[0]);
endmodule

module \Сумматор_с_памятью  (
  input  [7:0] A,
  input  [7:0] B,
  input  \Вычитание ,
  input  \Из_памяти ,
  output [7:0] out_5,
  output out_6
);

  wire \Записать_в_память_out , \Очистить_память_out ;
  wire [7:0] multiplexer_1_out, \n8_битный_регистр_1_out_5 ;

  // Probe on A
  // Probe on \n8_битный_регистр_1_out_5 
  Button \u_Записать_в_память  (.out(\Записать_в_память_out ));
  Button \u_Очистить_память  (.out(\Очистить_память_out ));
  Multiplexer #(.width(8)) multiplexer_1 (
    .in0(B), .in1(\n8_битный_регистр_1_out_5 ), .out(multiplexer_1_out), .sel(\Из_памяти ));  // open: en
  \_8_битный_сумматор  \u_8_битный_сумматор_1  (
    .in_2(multiplexer_1_out), .in_3(A), .out_5(out_5), .in_1(\Вычитание ), .out_4(out_6));
  \_8_битный_регистр  \u_8_битный_регистр_1  (
    .in_1(\Записать_в_память_out ), .in_2(out_5), .Enable(\Записать_в_память_out ),
    .Clear(\Очистить_память_out ), .out_5(\n8_битный_регистр_1_out_5 ));
  // Probe on out_5
  // Probe on out_5
endmodule

module \Аккумулятор  (
  input  [7:0] A,
  input  \Вычитание ,
  output [7:0] out_3,
  output out_4
);

  wire \Записать_в_память_out , \Очистить_память_out ;
  wire [7:0] \n8_битный_регистр_1_out_5 ;

  // Probe on A
  // Probe on \n8_битный_регистр_1_out_5 
  Button \u_Записать_в_память  (.out(\Записать_в_память_out ));
  Button \u_Очистить_память  (.out(\Очистить_память_out ));
  \_8_битный_сумматор  \u_8_битный_сумматор_1  (
    .in_2(\n8_битный_регистр_1_out_5 ), .in_3(A), .out_5(out_3), .in_1(\Вычитание ), .out_4(out_4));
  \_8_битный_регистр  \u_8_битный_регистр_1  (
    .in_1(\Записать_в_память_out ), .in_2(out_3), .Enable(\Записать_в_память_out ),
    .Clear(\Очистить_память_out ), .out_5(\n8_битный_регистр_1_out_5 ));
  // Probe on out_3
  // Probe on out_3
endmodule

module \Память  (
  input  [7:0] in_1,
  input  in_2,
  input  [2:0] in_3,
  output [7:0] out_4
);

  wire demultiplexer_1_out0, demultiplexer_1_out1, demultiplexer_1_out2, demultiplexer_1_out3,
       demultiplexer_1_out4, demultiplexer_1_out5, demultiplexer_1_out6, demultiplexer_1_out7;
  wire [7:0] register_1_q, register_2_q, register_3_q, register_4_q, register_5_q, register_6_q,
       register_7_q, register_8_q;

  Demultiplexer #(.select(3)) demultiplexer_1 (
    .out0(demultiplexer_1_out0), .out1(demultiplexer_1_out1), .out2(demultiplexer_1_out2),
    .out3(demultiplexer_1_out3), .out4(demultiplexer_1_out4), .out5(demultiplexer_1_out5),
    .out6(demultiplexer_1_out6), .out7(demultiplexer_1_out7), .in(in_2), .sel(in_3));  // open: en
  Register register_1 (.D(in_1), .Q(register_1_q), .clk(demultiplexer_1_out0));  // open: en, clr
  Register register_2 (.D(in_1), .Q(register_2_q), .clk(demultiplexer_1_out1));  // open: en, clr
  Register register_3 (.D(in_1), .Q(register_3_q), .clk(demultiplexer_1_out2));  // open: en, clr
  Register register_4 (.D(in_1), .Q(register_4_q), .clk(demultiplexer_1_out3));  // open: en, clr
  Register register_5 (.D(in_1), .Q(register_5_q), .clk(demultiplexer_1_out4));  // open: en, clr
  Register register_6 (.D(in_1), .Q(register_6_q), .clk(demultiplexer_1_out5));  // open: en, clr
  Register register_7 (.D(in_1), .Q(register_7_q), .clk(demultiplexer_1_out6));  // open: en, clr
  Register register_8 (.D(in_1), .Q(register_8_q), .clk(demultiplexer_1_out7));  // open: en, clr
  Multiplexer #(.select(3), .width(8)) multiplexer_1 (
    .in0(register_1_q), .in1(register_2_q), .in2(register_3_q), .in3(register_4_q), .in4(register_5_q),
    .in5(register_6_q), .in6(register_7_q), .in7(register_8_q), .out(out_4), .sel(in_3));  // open: en
endmodule

module \Память_синхронная  (
  input  [7:0] in_1,
  input  in_2,
  input  [1:0] in_3,
  output [7:0] out_4
);

  wire clock_1_out, demultiplexer_1_out0, demultiplexer_1_out1, demultiplexer_1_out2, demultiplexer_1_out3;
  wire [7:0] register_1_q, register_2_q, register_3_q, register_4_q;

  Demultiplexer #(.select(2)) demultiplexer_1 (
    .out0(demultiplexer_1_out0), .out1(demultiplexer_1_out1), .out2(demultiplexer_1_out2),
    .out3(demultiplexer_1_out3), .in(in_2), .sel(in_3));  // open: en
  Clock clock_1 (.out(clock_1_out));
  Register register_1 (.D(in_1), .en(demultiplexer_1_out0), .Q(register_1_q), .clk(clock_1_out));  // open: clr
  Register register_2 (.D(in_1), .en(demultiplexer_1_out1), .Q(register_2_q), .clk(clock_1_out));  // open: clr
  Register register_3 (.D(in_1), .en(demultiplexer_1_out2), .Q(register_3_q), .clk(clock_1_out));  // open: clr
  Register register_4 (.D(in_1), .en(demultiplexer_1_out3), .Q(register_4_q), .clk(clock_1_out));  // open: clr
  Multiplexer #(.select(2), .width(8)) multiplexer_1 (
    .in0(register_1_q), .in1(register_2_q), .in2(register_3_q), .in3(register_4_q), .out(out_4), .sel(in_3));  // open: en
endmodule

module _64x8 (
  input  [7:0] in_1,
  input  in_2,
  input  [2:0] in_3,
  input  [2:0] in_4,
  output [7:0] out_5
);

  wire demultiplexer_1_out0, demultiplexer_1_out1, demultiplexer_1_out2, demultiplexer_1_out3,
       demultiplexer_1_out4, demultiplexer_1_out5, demultiplexer_1_out6, demultiplexer_1_out7;
  wire [7:0] \память_1_out_4 , \память_2_out_4 , \память_3_out_4 , \память_4_out_4 , \память_5_out_4 ,
       \память_6_out_4 , \память_7_out_4 , \память_8_out_4 ;

  Demultiplexer #(.select(3)) demultiplexer_1 (
    .out0(demultiplexer_1_out0), .out1(demultiplexer_1_out1), .out2(demultiplexer_1_out2),
    .out3(demultiplexer_1_out3), .out4(demultiplexer_1_out4), .out5(demultiplexer_1_out5),
    .out6(demultiplexer_1_out6), .out7(demultiplexer_1_out7), .in(in_2), .sel(in_3));  // open: en
  \Память  \u_память_1  (.in_1(in_1), .in_2(demultiplexer_1_out0), .in_3(in_4), .out_4(\память_1_out_4 ));
  \Память  \u_память_2  (.in_1(in_1), .in_2(demultiplexer_1_out1), .in_3(in_4), .out_4(\память_2_out_4 ));
  \Память  \u_память_3  (.in_1(in_1), .in_2(demultiplexer_1_out2), .in_3(in_4), .out_4(\память_3_out_4 ));
  \Память  \u_память_4  (.in_1(in_1), .in_2(demultiplexer_1_out3), .in_3(in_4), .out_4(\память_4_out_4 ));
  \Память  \u_память_5  (.in_1(in_1), .in_2(demultiplexer_1_out4), .in_3(in_4), .out_4(\память_5_out_4 ));
  \Память  \u_память_6  (.in_1(in_1), .in_2(demultiplexer_1_out5), .in_3(in_4), .out_4(\память_6_out_4 ));
  \Память  \u_память_7  (.in_1(in_1), .in_2(demultiplexer_1_out6), .in_3(in_4), .out_4(\память_7_out_4 ));
  \Память  \u_память_8  (.in_1(in_1), .in_2(demultiplexer_1_out7), .in_3(in_4), .out_4(\память_8_out_4 ));
  Multiplexer #(.select(3), .width(8)) multiplexer_1 (
    .in0(\память_1_out_4 ), .in1(\память_2_out_4 ), .in2(\память_3_out_4 ), .in3(\память_4_out_4 ),
    .in4(\память_5_out_4 ), .in5(\память_6_out_4 ), .in6(\память_7_out_4 ), .in7(\память_8_out_4 ),
    .out(out_5), .sel(in_3));  // open: en
endmodule

module \_1024х8  (
  input  [7:0] in_1,
  input  in_2,
  input  [9:0] in_3,
  output [7:0] out_4
);

  wire demultiplexer_1_out0, demultiplexer_1_out1, demultiplexer_1_out2, demultiplexer_1_out3,
       demultiplexer_1_out4, demultiplexer_1_out5, demultiplexer_1_out6, demultiplexer_1_out7,
       demultiplexer_1_out8, demultiplexer_1_out9, demultiplexer_1_out10, demultiplexer_1_out11,
       demultiplexer_1_out12, demultiplexer_1_out13, demultiplexer_1_out14, demultiplexer_1_out15;
  wire [7:0] n64x8_1_out_5, n64x8_2_out_5, n64x8_3_out_5, n64x8_4_out_5, n64x8_5_out_5, n64x8_6_out_5,
       n64x8_7_out_5, n64x8_8_out_5, n64x8_9_out_5, n64x8_10_out_5, n64x8_11_out_5, n64x8_12_out_5,
       n64x8_13_out_5, n64x8_14_out_5, n64x8_15_out_5, n64x8_16_out_5;

  Demultiplexer #(.select(4)) demultiplexer_1 (
    .out0(demultiplexer_1_out0), .out1(demultiplexer_1_out1), .out2(demultiplexer_1_out2),
    .out3(demultiplexer_1_out3), .out4(demultiplexer_1_out4), .out5(demultiplexer_1_out5),
    .out6(demultiplexer_1_out6), .out7(demultiplexer_1_out7), .out8(demultiplexer_1_out8),
    .out9(demultiplexer_1_out9), .out10(demultiplexer_1_out10), .out11(demultiplexer_1_out11),
    .out12(demultiplexer_1_out12), .out13(demultiplexer_1_out13), .out14(demultiplexer_1_out14),
    .out15(demultiplexer_1_out15), .in(in_2), .sel(in_3[3:0]));  // open: en
  _64x8 u_64x8_1 (.in_1(in_1), .in_2(demultiplexer_1_out0), .in_3(in_3[9:7]), .in_4(in_3[6:4]), .out_5(n64x8_1_out_5));
  _64x8 u_64x8_2 (.in_1(in_1), .in_2(demultiplexer_1_out1), .in_3(in_3[9:7]), .in_4(in_3[6:4]), .out_5(n64x8_2_out_5));
  _64x8 u_64x8_3 (.in_1(in_1), .in_2(demultiplexer_1_out2), .in_3(in_3[9:7]), .in_4(in_3[6:4]), .out_5(n64x8_3_out_5));
  _64x8 u_64x8_4 (.in_1(in_1), .in_2(demultiplexer_1_out3), .in_3(in_3[9:7]), .in_4(in_3[6:4]), .out_5(n64x8_4_out_5));
  _64x8 u_64x8_5 (.in_1(in_1), .in_2(demultiplexer_1_out4), .in_3(in_3[9:7]), .in_4(in_3[6:4]), .out_5(n64x8_5_out_5));
  _64x8 u_64x8_6 (.in_1(in_1), .in_2(demultiplexer_1_out5), .in_3(in_3[9:7]), .in_4(in_3[6:4]), .out_5(n64x8_6_out_5));
  _64x8 u_64x8_7 (.in_1(in_1), .in_2(demultiplexer_1_out6), .in_3(in_3[9:7]), .in_4(in_3[6:4]), .out_5(n64x8_7_out_5));
  _64x8 u_64x8_8 (.in_1(in_1), .in_2(demultiplexer_1_out7), .in_3(in_3[9:7]), .in_4(in_3[6:4]), .out_5(n64x8_8_out_5));
  _64x8 u_64x8_9 (.in_1(in_1), .in_2(demultiplexer_1_out8), .in_3(in_3[9:7]), .in_4(in_3[6:4]), .out_5(n64x8_9_out_5));
  _64x8 u_64x8_10 (
    .in_1(in_1), .in_2(demultiplexer_1_out9), .in_3(in_3[9:7]), .in_4(in_3[6:4]), .out_5(n64x8_10_out_5));
  _64x8 u_64x8_11 (
    .in_1(in_1), .in_2(demultiplexer_1_out10), .in_3(in_3[9:7]), .in_4(in_3[6:4]), .out_5(n64x8_11_out_5));
  _64x8 u_64x8_12 (
    .in_1(in_1), .in_2(demultiplexer_1_out11), .in_3(in_3[9:7]), .in_4(in_3[6:4]), .out_5(n64x8_12_out_5));
  _64x8 u_64x8_13 (
    .in_1(in_1), .in_2(demultiplexer_1_out12), .in_3(in_3[9:7]), .in_4(in_3[6:4]), .out_5(n64x8_13_out_5));
  _64x8 u_64x8_14 (
    .in_1(in_1), .in_2(demultiplexer_1_out13), .in_3(in_3[9:7]), .in_4(in_3[6:4]), .out_5(n64x8_14_out_5));
  _64x8 u_64x8_15 (
    .in_1(in_1), .in_2(demultiplexer_1_out14), .in_3(in_3[9:7]), .in_4(in_3[6:4]), .out_5(n64x8_15_out_5));
  _64x8 u_64x8_16 (
    .in_1(in_1), .in_2(demultiplexer_1_out15), .in_3(in_3[9:7]), .in_4(in_3[6:4]), .out_5(n64x8_16_out_5));
  Multiplexer #(.select(4), .width(8)) multiplexer_1 (
    .in0(n64x8_1_out_5), .in1(n64x8_2_out_5), .in2(n64x8_3_out_5), .in3(n64x8_4_out_5), .in4(n64x8_5_out_5),
    .in5(n64x8_6_out_5), .in6(n64x8_7_out_5), .in7(n64x8_8_out_5), .in8(n64x8_9_out_5), .in9(n64x8_10_out_5),
    .in10(n64x8_11_out_5), .in11(n64x8_12_out_5), .in12(n64x8_13_out_5), .in13(n64x8_14_out_5),
    .in14(n64x8_15_out_5), .in15(n64x8_16_out_5), .out(out_4), .sel(in_3[3:0]));  // open: en
endmodule
