// Logisim project Триггеры.circ as structural Verilog: 22 circuits, main circuit D-тгриггер с очисткой по верхнему уровню
module \RS_триггер  (
  input  RESET,
  input  SET,
  output out_3,
  output out_4
);

  nor nor_1 (out_3, RESET, out_4);
  nor nor_2 (out_4, out_3, SET);
endmodule

module \JK___триггер  (
  input  K,
  input  C,
  input  J,
  output Q,
  output not_Q
);

  wire and_1_out, and_2_out, s_r_ff_1_q, s_r_ff_1_qn;

  and and_1 (and_1_out, Q, K);
  and and_2 (and_2_out, J, not_Q);
  S_R_Flip_Flop s_r_ff_1 (
    .S(and_2_out), .clk(C), .R(and_1_out), .Q(s_r_ff_1_q), .Qn(s_r_ff_1_qn));  // open: preset, reset, en
  not not_1 (s_r_ff_1_qn, C);
  S_R_Flip_Flop s_r_ff_2 (
    .S(s_r_ff_1_qn), .clk(s_r_ff_1_qn), .R(s_r_ff_1_q), .Q(Q), .Qn(not_Q));  // open: preset, reset, en
endmodule

module \D_триггер_с_предустановкой_и_очисткой__сраьатывающий_по_фронту  (
  input  CLEAR,
  input  SET_1,
  input  CLOCK,
  input  DATA,
  output Q,
  output NOT_Q
);

  wire nor_1_out, nor_2_out, nor_3_out, nor_4_out, not_1_out;

  not not_1 (not_1_out, CLOCK);
  nor nor_1 (nor_1_out, CLEAR, nor_4_out, nor_2_out);
  nor nor_2 (nor_2_out, nor_1_out, SET_1, not_1_out);
  nor nor_3 (nor_3_out, nor_2_out, not_1_out, nor_4_out);
  nor nor_4 (nor_4_out, nor_3_out, SET_1, DATA);
  nor nor_5 (Q, CLEAR, nor_2_out, NOT_Q);
  nor nor_6 (NOT_Q, Q, SET_1, nor_3_out);
endmodule

module \D_тгриггер_с_очисткой_по_верхнему_уровню  (
  input  CLEAR,
  input  CLOCK,
  input  PRESET,
  input  DATA,
  input  DATA_2,
  input  \Всегда_1 ,
  input  \Питание ,
  input  \Всегда_0 ,
  output Q,
  output nQ,
  output out_11
);

  wire and_1_out, and_2_out, not_1_out, or_1_out, \Тактовый_генератор_out ;

  not not_1 (not_1_out, DATA);
  and and_1 (and_1_out, not_1_out, CLOCK);
  and and_2 (and_2_out, CLOCK, DATA);
  Clock \u_Тактовый_генератор  (.out(\Тактовый_генератор_out ));
  D_Flip_Flop d_ff_1 (
    .clk(\Тактовый_генератор_out ), .D(DATA_2), .Qn(out_11), .preset(\Всегда_1 ), .en(\Питание ),
    .reset(\Всегда_0 ));  // open: Q
  or or_1 (or_1_out, CLEAR, and_1_out);
  nor nor_1 (Q, or_1_out, nQ);
  nor nor_2 (nQ, Q, PRESET, and_2_out);
endmodule

module \D_триггер_по_нижнему_уровню  (
  input  CLEAR,
  input  CLOCK,
  input  PRESET,
  input  DATA,
  output Q,
  output nQ
);

  wire and_1_out, and_2_out, not_1_out, not_2_out, or_1_out;

  not not_1 (not_1_out, DATA);
  and and_1 (and_1_out, not_1_out, not_2_out);
  not not_2 (not_2_out, CLOCK);
  and and_2 (and_2_out, not_2_out, DATA);
  or or_1 (or_1_out, CLEAR, and_1_out);
  nor nor_1 (Q, or_1_out, nQ);
  nor nor_2 (nQ, Q, PRESET, and_2_out);
endmodule

module \D___триггер_по_фронту  (
  input  CLEAR,
  input  DATE,
  input  CLOCK,
  input  PRESET,
  output Q,
  output nQ
);

  wire and_1_out, and_2_out, and_3_out, and_4_out, nor_1_out, nor_2_out, not_1_out;

  not not_1 (not_1_out, CLOCK);
  and and_1 (and_1_out, DATE, not_1_out);
  and and_2 (and_2_out, not_1_out, ~DATE);  // AND_Gate
  nor nor_1 (nor_1_out, CLEAR, and_1_out, nor_2_out);
  nor nor_2 (nor_2_out, nor_1_out, and_2_out);
  and and_3 (and_3_out, nor_1_out, CLOCK);
  and and_4 (and_4_out, CLOCK, nor_2_out);
  nor nor_3 (Q, CLEAR, and_3_out, nQ);
  nor nor_4 (nQ, Q, PRESET, and_4_out);
endmodule

module \D___триггер_по_заднему_фронту  (
  input  CLEAR,
  input  DATE,
  input  CLOCK,
  input  PRESET,
  output Q,
  output nQ
);

  wire and_1_out, and_2_out, and_3_out, and_4_out, nor_1_out, nor_2_out, not_1_out;

  not not_1 (not_1_out, CLOCK);
  and and_1 (and_1_out, DATE, CLOCK);
  and and_2 (and_2_out, CLOCK, ~DATE);  // AND_Gate
  nor nor_1 (nor_1_out, and_1_out, PRESET, nor_2_out);
  nor nor_2 (nor_2_out, nor_1_out, CLEAR, and_2_out);
  and and_3 (and_3_out, nor_1_out, not_1_out);
  and and_4 (and_4_out, not_1_out, nor_2_out);
  nor nor_3 (Q, CLEAR, and_3_out, nQ);
  nor nor_4 (nQ, Q, PRESET, and_4_out);
endmodule

module \RS__D____триггер  (
  input  R,
  input  S,
  input  C,
  output Q,
  output nQ
);

  wire and_1_out, or_1_out;

  and and_1 (and_1_out, Q, ~R);  // AND_Gate
  or or_1 (or_1_out, and_1_out, S);
  D_Flip_Flop d_ff_1 (.clk(C), .D(or_1_out), .Q(Q), .Qn(nQ));  // open: preset, en, reset
endmodule

module \RS__JK____триггер  (
  input  S,
  input  C,
  input  R,
  output out_4,
  output out_5
);

  J_K_Flip_Flop j_k_ff_1 (.J(S), .clk(C), .K(R), .Q(out_4), .Qn(out_5));  // open: preset, en, reset
endmodule

module \RS__TC____триггер  (
  input  C,
  input  R,
  input  S,
  output out_4,
  output out_5
);

  wire and_1_out, and_2_out, or_1_out;

  and and_1 (and_1_out, out_4, R);
  and and_2 (and_2_out, S, out_5);
  or or_1 (or_1_out, and_1_out, and_2_out);
  T_Flip_Flop t_ff_1 (.clk(C), .T(or_1_out), .Q(out_4), .Qn(out_5));  // open: preset, reset, en
endmodule

module \D__RS____триггер  (
  input  C,
  input  D,
  output Q,
  output not_Q
);

  wire not_1_out;

  not not_1 (not_1_out, C);
  S_R_Flip_Flop s_r_ff_1 (.S(C), .clk(D), .R(not_1_out), .Q(Q), .Qn(not_Q));  // open: preset, reset, en
endmodule

module \D__JK____триггер  (
  input  D,
  input  C,
  output out_3,
  output out_4
);

  wire not_1_out;

  J_K_Flip_Flop j_k_ff_1 (.J(D), .clk(C), .K(not_1_out), .Q(out_3), .Qn(out_4));  // open: preset, en, reset
  not not_1 (not_1_out, D);
endmodule

module \D__TC____триггер  (
  input  C,
  input  D,
  output Q,
  output nQ
);

  wire xor_1_out;

  xor xor_1 (xor_1_out, D, Q);
  T_Flip_Flop t_ff_1 (.clk(C), .T(xor_1_out), .Q(Q), .Qn(nQ));  // open: preset, reset, en
endmodule

module \JK__RS____триггер  (
  input  K,
  input  J,
  input  C,
  output out_4,
  output out_5
);

  wire and_1_out, and_2_out;

  and and_1 (and_1_out, out_4, K);
  and and_2 (and_2_out, J, out_5);
  S_R_Flip_Flop s_r_ff_1 (.S(and_2_out), .clk(C), .R(and_1_out), .Q(out_4), .Qn(out_5));  // open: preset, reset, en
endmodule

module \JK__D____триггер  (
  input  K,
  input  J,
  input  C,
  output out_4,
  output out_5
);

  wire and_1_out, and_2_out, or_1_out;

  and and_1 (and_1_out, out_4, ~K);  // AND_Gate
  and and_2 (and_2_out, J, out_5);
  or or_1 (or_1_out, and_1_out, and_2_out);
  D_Flip_Flop d_ff_1 (.clk(C), .D(or_1_out), .Q(out_4), .Qn(out_5));  // open: preset, en, reset
endmodule

module \JK__TC____триггер  (
  input  C,
  input  K,
  input  J,
  output out_4,
  output out_5
);

  wire and_1_out, and_2_out, or_1_out;

  and and_1 (and_1_out, K, out_4);
  and and_2 (and_2_out, out_5, J);
  or or_1 (or_1_out, and_1_out, and_2_out);
  T_Flip_Flop t_ff_1 (.clk(C), .T(or_1_out), .Q(out_4), .Qn(out_5));  // open: preset, reset, en
endmodule

module \TC__RS____триггер  (
  input  T,
  input  C,
  output Q,
  output not_Q
);

  wire not_1_out, xor_1_out;

  xor xor_1 (xor_1_out, Q, T);
  S_R_Flip_Flop s_r_ff_1 (.S(xor_1_out), .clk(C), .R(not_1_out), .Q(Q), .Qn(not_Q));  // open: preset, reset, en
  not not_1 (not_1_out, xor_1_out);
endmodule

module \TC__D____триггеры  (
  input  T,
  input  C,
  output out_3
);

  wire d_ff_1_q, xor_1_out;

  xor xor_1 (xor_1_out, d_ff_1_q, T);
  D_Flip_Flop d_ff_1 (.clk(C), .D(xor_1_out), .Q(d_ff_1_q), .Qn(out_3));  // open: preset, en, reset
endmodule

module \TC__JK____триггер  (
  input  T,
  input  C,
  output out_3,
  output out_4
);

  J_K_Flip_Flop j_k_ff_1 (.J(T), .clk(C), .K(T), .Q(out_3), .Qn(out_4));  // open: preset, en, reset
endmodule

module \T__RS____триггер  (
  input  T,
  output out_2,
  output out_3
);

  S_R_Flip_Flop s_r_ff_1 (.S(out_3), .clk(T), .R(out_2), .Q(out_2), .Qn(out_3));  // open: preset, reset, en
endmodule

module \T__D____триггер  (
  input  T,
  output out_2,
  output out_3
);

  D_Flip_Flop d_ff_1 (.clk(T), .D(out_3), .Q(out_2), .Qn(out_3));  // open: preset, en, reset
endmodule

module \T__JK____триггер  (
  input  R,
  output out_2,
  output out_3
);

  J_K_Flip_Flop j_k_ff_1 (.J(1'b1), .clk(R), .K(1'b1), .Q(out_2), .Qn(out_3));  // open: preset, en, reset
endmodule
