// Logisim project Доп_материалы Шифратор, дешифратор.circ as structural Verilog: 5 circuits, main circuit Шифратор 0-9 В1
module \Шифратор_0_9_В1  (
  input  x9,
  input  x8,
  input  x7,
  input  x6,
  input  x5,
  input  x4,
  input  x3,
  input  x2,
  input  x1,
  input  x0,
  output [3:0] out_11,
  output M
);

  wire and_1_out, and_2_out, and_3_out, and_4_out, and_5_out, and_6_out, and_7_out, and_8_out, and_9_out,
       and_10_out, and_11_out, and_12_out, and_13_out, and_14_out, and_15_out, and_16_out, and_17_out,
       and_18_out, and_19_out, and_20_out, and_21_out, and_22_out, and_23_out, and_24_out, and_25_out,
       and_26_out, and_27_out, and_28_out, and_29_out, and_30_out, and_31_out, and_32_out, and_33_out,
       and_34_out, and_35_out, and_36_out, and_37_out, and_38_out, and_39_out, and_40_out, and_41_out,
       and_42_out, and_43_out, and_44_out, and_45_out, and_46_out, and_47_out, and_48_out, and_49_out,
       and_50_out, and_51_out, and_52_out, and_53_out, and_54_out, and_55_out, and_56_out, and_57_out,
       and_58_out, and_59_out, and_60_out, and_61_out, not_1_out, not_2_out, not_3_out, not_4_out, not_5_out,
       not_6_out, not_7_out, not_8_out, not_9_out, not_10_out, not_11_out, not_12_out, not_13_out,
       not_14_out, not_15_out, not_16_out, not_17_out, not_18_out, not_19_out, not_20_out, not_21_out,
       not_22_out, not_23_out, not_24_out, not_25_out, not_26_out, not_27_out, not_28_out, not_29_out,
       not_30_out, not_31_out, not_32_out, not_33_out, not_34_out, not_35_out, not_36_out, not_37_out,
       not_38_out, not_39_out, not_40_out, not_41_out, not_42_out, not_43_out, not_44_out, not_45_out,
       not_46_out, not_47_out, not_48_out, not_49_out, not_50_out, not_51_out, not_52_out, not_53_out,
       not_54_out, not_55_out, not_56_out, not_57_out, not_58_out, not_59_out, not_60_out, not_61_out,
       not_62_out, not_63_out, not_64_out, not_65_out, not_66_out, not_67_out, not_68_out, not_69_out,
       not_70_out, not_71_out, not_72_out, not_73_out, not_74_out, not_75_out, not_76_out, not_77_out,
       not_78_out, not_79_out, not_80_out, not_81_out, not_82_out, not_83_out, not_84_out, not_85_out,
       not_86_out, not_87_out, not_88_out, not_89_out, not_90_out, not_91_out, not_92_out, not_93_out,
       not_94_out, not_95_out, not_96_out, not_97_out, not_98_out, not_99_out, not_100_out, not_101_out,
       not_102_out, not_103_out, not_104_out, not_105_out, not_106_out, not_107_out, not_108_out,
       not_109_out, not_110_out, not_111_out, not_112_out, not_113_out, not_114_out, not_115_out,
       not_116_out, not_117_out, not_118_out, not_119_out, not_120_out, not_121_out, not_122_out,
       not_123_out, not_124_out, not_125_out, not_126_out, not_127_out, not_128_out, not_129_out,
       not_130_out, not_131_out, not_132_out, not_133_out, not_134_out, not_135_out, not_136_out,
       not_137_out, not_138_out, not_139_out, not_140_out, not_141_out, not_142_out, not_143_out,
       not_144_out, not_145_out, or_5_out, or_6_out;

  not not_1 (not_1_out, x9);
  not not_2 (not_2_out, x7);
  not not_3 (not_3_out, x6);
  not not_4 (not_4_out, x5);
  not not_5 (not_5_out, x4);
  not not_6 (not_6_out, x3);
  not not_7 (not_7_out, x2);
  not not_8 (not_8_out, x1);
  not not_9 (not_9_out, x0);
  not not_10 (not_10_out, x8);
  not not_11 (not_11_out, x7);
  not not_12 (not_12_out, x6);
  not not_13 (not_13_out, x5);
  not not_14 (not_14_out, x4);
  not not_15 (not_15_out, x3);
  not not_16 (not_16_out, x2);
  not not_17 (not_17_out, x1);
  not not_18 (not_18_out, x0);
  not not_19 (not_19_out, x9);
  not not_20 (not_20_out, x8);
  not not_21 (not_21_out, x7);
  not not_22 (not_22_out, x6);
  not not_23 (not_23_out, x5);
  not not_24 (not_24_out, x3);
  not not_25 (not_25_out, x2);
  not not_26 (not_26_out, x1);
  not not_27 (not_27_out, x0);
  not not_28 (not_28_out, x9);
  not not_29 (not_29_out, x8);
  not not_30 (not_30_out, x7);
  not not_31 (not_31_out, x6);
  not not_32 (not_32_out, x4);
  not not_33 (not_33_out, x3);
  not not_34 (not_34_out, x2);
  not not_35 (not_35_out, x1);
  not not_36 (not_36_out, x0);
  not not_37 (not_37_out, x9);
  not not_38 (not_38_out, x8);
  not not_39 (not_39_out, x7);
  not not_40 (not_40_out, x5);
  not not_41 (not_41_out, x4);
  not not_42 (not_42_out, x3);
  not not_43 (not_43_out, x2);
  not not_44 (not_44_out, x1);
  not not_45 (not_45_out, x0);
  not not_46 (not_46_out, x9);
  not not_47 (not_47_out, x8);
  not not_48 (not_48_out, x6);
  not not_49 (not_49_out, x5);
  not not_50 (not_50_out, x4);
  not not_51 (not_51_out, x3);
  not not_52 (not_52_out, x2);
  not not_53 (not_53_out, x1);
  not not_54 (not_54_out, x0);
  not not_55 (not_55_out, x9);
  not not_56 (not_56_out, x8);
  not not_57 (not_57_out, x7);
  not not_58 (not_58_out, x6);
  not not_59 (not_59_out, x5);
  not not_60 (not_60_out, x4);
  not not_61 (not_61_out, x3);
  not not_62 (not_62_out, x1);
  not not_63 (not_63_out, x0);
  not not_64 (not_64_out, x9);
  not not_65 (not_65_out, x8);
  not not_66 (not_66_out, x7);
  not not_67 (not_67_out, x6);
  not not_68 (not_68_out, x5);
  not not_69 (not_69_out, x4);
  not not_70 (not_70_out, x2);
  not not_71 (not_71_out, x1);
  not not_72 (not_72_out, x0);
  not not_73 (not_73_out, x9);
  not not_74 (not_74_out, x8);
  not not_75 (not_75_out, x7);
  not not_76 (not_76_out, x5);
  not not_77 (not_77_out, x4);
  not not_78 (not_78_out, x3);
  not not_79 (not_79_out, x2);
  not not_80 (not_80_out, x1);
  not not_81 (not_81_out, x0);
  not not_82 (not_82_out, x9);
  not not_83 (not_83_out, x8);
  not not_84 (not_84_out, x6);
  not not_85 (not_85_out, x5);
  not not_86 (not_86_out, x4);
  not not_87 (not_87_out, x3);
  not not_88 (not_88_out, x2);
  not not_89 (not_89_out, x1);
  not not_90 (not_90_out, x0);
  not not_91 (not_91_out, x9);
  not not_92 (not_92_out, x8);
  not not_93 (not_93_out, x7);
  not not_94 (not_94_out, x6);
  not not_95 (not_95_out, x5);
  not not_96 (not_96_out, x4);
  not not_97 (not_97_out, x3);
  not not_98 (not_98_out, x2);
  not not_99 (not_99_out, x0);
  not not_100 (not_100_out, x9);
  not not_101 (not_101_out, x8);
  not not_102 (not_102_out, x7);
  not not_103 (not_103_out, x6);
  not not_104 (not_104_out, x5);
  not not_105 (not_105_out, x4);
  not not_106 (not_106_out, x2);
  not not_107 (not_107_out, x1);
  not not_108 (not_108_out, x0);
  not not_109 (not_109_out, x9);
  not not_110 (not_110_out, x8);
  not not_111 (not_111_out, x7);
  not not_112 (not_112_out, x6);
  not not_113 (not_113_out, x4);
  not not_114 (not_114_out, x3);
  not not_115 (not_115_out, x2);
  not not_116 (not_116_out, x1);
  not not_117 (not_117_out, x0);
  not not_118 (not_118_out, x9);
  not not_119 (not_119_out, x8);
  not not_120 (not_120_out, x6);
  not not_121 (not_121_out, x5);
  not not_122 (not_122_out, x4);
  not not_123 (not_123_out, x3);
  not not_124 (not_124_out, x2);
  not not_125 (not_125_out, x1);
  not not_126 (not_126_out, x0);
  not not_127 (not_127_out, x8);
  not not_128 (not_128_out, x7);
  not not_129 (not_129_out, x6);
  not not_130 (not_130_out, x5);
  not not_131 (not_131_out, x4);
  not not_132 (not_132_out, x3);
  not not_133 (not_133_out, x2);
  not not_134 (not_134_out, x1);
  not not_135 (not_135_out, x0);
  not not_136 (not_136_out, x9);
  not not_137 (not_137_out, x8);
  not not_138 (not_138_out, x7);
  not not_139 (not_139_out, x6);
  not not_140 (not_140_out, x5);
  not not_141 (not_141_out, x4);
  not not_142 (not_142_out, x3);
  not not_143 (not_143_out, x2);
  not not_144 (not_144_out, x1);
  not not_145 (not_145_out, x0);
  and and_1 (and_1_out, not_1_out, x8, not_2_out, not_3_out, not_4_out, not_5_out, not_6_out, not_7_out, not_8_out, not_9_out);
  and and_2 (and_2_out, x9, not_10_out, not_11_out, not_12_out, not_13_out, not_14_out, not_15_out, not_16_out, not_17_out, not_18_out);
  and and_3 (and_3_out, not_19_out, not_20_out, not_21_out, not_22_out, not_23_out, x4, not_24_out, not_25_out, not_26_out, not_27_out);
  and and_4 (and_4_out, not_28_out, not_29_out, not_30_out, not_31_out, x5, not_32_out, not_33_out, not_34_out, not_35_out, not_36_out);
  and and_5 (and_5_out, not_37_out, not_38_out, not_39_out, x6, not_40_out, not_41_out, not_42_out, not_43_out, not_44_out, not_45_out);
  and and_6 (and_6_out, not_46_out, not_47_out, x7, not_48_out, not_49_out, not_50_out, not_51_out, not_52_out, not_53_out, not_54_out);
  and and_7 (and_7_out, not_55_out, not_56_out, not_57_out, not_58_out, not_59_out, not_60_out, not_61_out, x2, not_62_out, not_63_out);
  and and_8 (and_8_out, not_64_out, not_65_out, not_66_out, not_67_out, not_68_out, not_69_out, x3, not_70_out, not_71_out, not_72_out);
  and and_9 (and_9_out, not_73_out, not_74_out, not_75_out, x6, not_76_out, not_77_out, not_78_out, not_79_out, not_80_out, not_81_out);
  and and_10 (and_10_out, not_82_out, not_83_out, x7, not_84_out, not_85_out, not_86_out, not_87_out, not_88_out, not_89_out, not_90_out);
  and and_11 (and_11_out, not_91_out, not_92_out, not_93_out, not_94_out, not_95_out, not_96_out, not_97_out, not_98_out, x1, not_99_out);
  and and_12 (and_12_out, not_100_out, not_101_out, not_102_out, not_103_out, not_104_out, not_105_out, x3, not_106_out, not_107_out, not_108_out);
  and and_13 (and_13_out, not_109_out, not_110_out, not_111_out, not_112_out, x5, not_113_out, not_114_out, not_115_out, not_116_out, not_117_out);
  and and_14 (and_14_out, not_118_out, not_119_out, x7, not_120_out, not_121_out, not_122_out, not_123_out, not_124_out, not_125_out, not_126_out);
  and and_15 (and_15_out, x9, not_127_out, not_128_out, not_129_out, not_130_out, not_131_out, not_132_out, not_133_out, not_134_out, not_135_out);
  and and_16 (and_16_out, not_136_out, not_137_out, not_138_out, not_139_out, not_140_out, not_141_out, not_142_out, not_143_out, not_144_out, not_145_out);
  and and_17 (and_17_out, x1, x0);
  and and_18 (and_18_out, x2, x0);
  and and_19 (and_19_out, x2, x1);
  and and_20 (and_20_out, x3, x0);
  and and_21 (and_21_out, x3, x1);
  and and_22 (and_22_out, x3, x2);
  and and_23 (and_23_out, x4, x0);
  and and_24 (and_24_out, x4, x1);
  and and_25 (and_25_out, x4, x2);
  and and_26 (and_26_out, x4, x3);
  and and_27 (and_27_out, x5, x0);
  and and_28 (and_28_out, x5, x1);
  and and_29 (and_29_out, x5, x2);
  and and_30 (and_30_out, x5, x3);
  and and_31 (and_31_out, x5, x4);
  and and_32 (and_32_out, x6, x0);
  and and_33 (and_33_out, x6, x1);
  and and_34 (and_34_out, x6, x2);
  and and_35 (and_35_out, x6, x3);
  and and_36 (and_36_out, x6, x4);
  and and_37 (and_37_out, x6, x5);
  and and_38 (and_38_out, x7, x0);
  and and_39 (and_39_out, x7, x1);
  and and_40 (and_40_out, x7, x2);
  and and_41 (and_41_out, x7, x3);
  and and_42 (and_42_out, x7, x4);
  and and_43 (and_43_out, x7, x5);
  and and_44 (and_44_out, x7, x6);
  and and_45 (and_45_out, x8, x0);
  and and_46 (and_46_out, x8, x1);
  and and_47 (and_47_out, x8, x2);
  and and_48 (and_48_out, x8, x3);
  and and_49 (and_49_out, x8, x4);
  and and_50 (and_50_out, x8, x5);
  and and_51 (and_51_out, x8, x6);
  and and_52 (and_52_out, x8, x7);
  and and_53 (and_53_out, x9, x0);
  and and_54 (and_54_out, x9, x1);
  and and_55 (and_55_out, x9, x2);
  and and_56 (and_56_out, x9, x3);
  and and_57 (and_57_out, x9, x4);
  and and_58 (and_58_out, x9, x5);
  and and_59 (and_59_out, x9, x6);
  and and_60 (and_60_out, x9, x7);
  and and_61 (and_61_out, x9, x8);
  or or_1 (out_11[3], and_1_out, and_2_out);
  or or_2 (out_11[2], and_3_out, and_4_out, and_5_out, and_6_out);
  or or_3 (out_11[1], and_7_out, and_8_out, and_9_out, and_10_out);
  or or_4 (out_11[0], and_11_out, and_12_out, and_13_out, and_14_out, and_15_out);
  or or_5 (or_5_out, and_16_out, and_17_out, and_18_out, and_19_out, and_20_out, and_21_out, and_22_out, and_23_out, and_24_out, and_25_out, and_26_out, and_27_out, and_28_out, and_29_out, and_30_out, and_31_out, and_32_out, and_33_out, and_34_out, and_35_out, and_36_out, and_37_out, and_38_out);
  or or_6 (or_6_out, and_39_out, and_40_out, and_41_out, and_42_out, and_43_out, and_44_out, and_45_out, and_46_out, and_47_out, and_48_out, and_49_out, and_50_out, and_51_out, and_52_out, and_53_out, and_54_out, and_55_out, and_56_out, and_57_out, and_58_out, and_59_out, and_60_out, and_61_out);
  or or_7 (M, or_5_out, or_6_out);
endmodule

module \Дешифратор_0_9  (
  input  x3,
  input  x2,
  input  x1,
  input  x0,
  output y7,
  output y6,
  output y5,
  output y4,
  output y3,
  output y2,
  output y1,
  output y0,
  output M
);

  wire and_1_out, and_2_out, and_3_out, and_4_out, and_5_out, and_6_out, and_7_out, and_8_out, and_9_out,
       and_10_out, and_11_out, and_12_out, and_13_out, and_14_out, and_15_out, and_16_out, and_17_out,
       and_18_out, and_19_out, and_20_out, and_21_out, and_22_out, and_23_out, and_24_out, and_25_out,
       and_26_out, and_27_out, and_28_out, and_29_out, and_30_out, not_1_out, not_2_out, not_3_out,
       not_4_out, not_5_out, not_6_out, not_7_out, not_8_out, not_9_out, not_10_out, not_11_out, not_12_out,
       not_13_out, not_14_out, not_15_out, not_16_out, not_17_out, not_18_out, not_19_out, not_20_out,
       not_21_out, not_22_out, not_23_out, not_24_out, not_25_out, not_26_out, not_27_out, not_28_out,
       not_29_out, not_30_out, not_31_out, not_32_out, not_33_out, not_34_out, not_35_out, not_36_out,
       not_37_out, not_38_out, not_39_out, not_40_out, not_41_out, not_42_out, not_43_out, not_44_out,
       not_45_out, not_46_out, not_47_out, not_48_out, not_49_out, not_50_out, not_51_out, not_52_out,
       not_53_out, not_54_out, not_55_out, not_56_out;

  not not_1 (not_1_out, x3);
  not not_2 (not_2_out, x0);
  not not_3 (not_3_out, x2);
  not not_4 (not_4_out, x1);
  not not_5 (not_5_out, x2);
  and and_1 (and_1_out, not_5_out, not_6_out);
  not not_6 (not_6_out, x1);
  not not_7 (not_7_out, x3);
  and and_2 (and_2_out, not_7_out, x0);
  not not_8 (not_8_out, x3);
  and and_3 (and_3_out, not_8_out, x2);
  not not_9 (not_9_out, x3);
  not not_10 (not_10_out, x2);
  not not_11 (not_11_out, x0);
  not not_12 (not_12_out, x3);
  not not_13 (not_13_out, x2);
  not not_14 (not_14_out, x3);
  not not_15 (not_15_out, x0);
  not not_16 (not_16_out, x3);
  not not_17 (not_17_out, x1);
  not not_18 (not_18_out, x2);
  not not_19 (not_19_out, x1);
  not not_20 (not_20_out, x2);
  not not_21 (not_21_out, x1);
  and and_4 (and_4_out, not_20_out, not_21_out, not_22_out);
  not not_22 (not_22_out, x0);
  not not_23 (not_23_out, x3);
  and and_5 (and_5_out, not_23_out, x1, not_24_out);
  not not_24 (not_24_out, x0);
  not not_25 (not_25_out, x3);
  and and_6 (and_6_out, not_25_out, not_26_out, x1);
  not not_26 (not_26_out, x2);
  not not_27 (not_27_out, x3);
  and and_7 (and_7_out, not_27_out, x2, not_28_out);
  not not_28 (not_28_out, x1);
  not not_29 (not_29_out, x3);
  and and_8 (and_8_out, not_29_out, x2, not_30_out);
  not not_30 (not_30_out, x0);
  not not_31 (not_31_out, x2);
  and and_9 (and_9_out, x3, not_31_out, not_32_out);
  not not_32 (not_32_out, x1);
  not not_33 (not_33_out, x3);
  not not_34 (not_34_out, x1);
  and and_10 (and_10_out, not_33_out, not_34_out, not_35_out);
  not not_35 (not_35_out, x0);
  not not_36 (not_36_out, x3);
  and and_11 (and_11_out, not_36_out, x2, not_37_out);
  not not_37 (not_37_out, x1);
  not not_38 (not_38_out, x3);
  and and_12 (and_12_out, not_38_out, x2, not_39_out);
  not not_39 (not_39_out, x0);
  and and_13 (and_13_out, x3, not_40_out, not_41_out);
  not not_40 (not_40_out, x2);
  not not_41 (not_41_out, x1);
  not not_42 (not_42_out, x3);
  not not_43 (not_43_out, x2);
  and and_14 (and_14_out, not_42_out, not_43_out, not_44_out);
  not not_44 (not_44_out, x0);
  not not_45 (not_45_out, x3);
  and and_15 (and_15_out, not_45_out, x1);
  not not_46 (not_46_out, x3);
  and and_16 (and_16_out, not_46_out, x2, x0);
  not not_47 (not_47_out, x2);
  and and_17 (and_17_out, x3, not_47_out, not_48_out);
  not not_48 (not_48_out, x1);
  not not_49 (not_49_out, x3);
  and and_18 (and_18_out, not_49_out, not_50_out);
  not not_50 (not_50_out, x2);
  not not_51 (not_51_out, x3);
  not not_52 (not_52_out, x1);
  and and_19 (and_19_out, not_51_out, not_52_out, not_53_out);
  not not_53 (not_53_out, x0);
  not not_54 (not_54_out, x2);
  and and_20 (and_20_out, not_54_out, not_55_out);
  not not_55 (not_55_out, x1);
  not not_56 (not_56_out, x3);
  and and_21 (and_21_out, not_56_out, x1, x0);
  and and_22 (and_22_out, x3, x1);
  and and_23 (and_23_out, x3, x2);
  and and_24 (and_24_out, not_1_out, x2, x1, not_2_out);
  or or_1 (y7, and_24_out, and_25_out);
  and and_25 (and_25_out, x3, not_3_out, not_4_out, x0);
  or or_2 (y6, and_1_out, and_2_out, and_3_out);
  and and_26 (and_26_out, not_9_out, not_10_out, not_11_out);
  and and_27 (and_27_out, not_12_out, not_13_out, x1);
  and and_28 (and_28_out, not_14_out, x1, not_15_out);
  and and_29 (and_29_out, not_16_out, x2, not_17_out, x0);
  and and_30 (and_30_out, x3, not_18_out, not_19_out);
  or or_3 (y4, and_4_out, and_5_out);
  or or_4 (y3, and_6_out, and_7_out, and_8_out, and_9_out);
  or or_5 (y2, and_10_out, and_11_out, and_12_out, and_13_out);
  or or_6 (y1, and_14_out, and_15_out, and_16_out, and_17_out);
  or or_7 (y0, and_18_out, and_19_out, and_20_out, and_21_out);
  or or_8 (M, and_22_out, and_23_out);
  or or_9 (y5, and_26_out, and_27_out, and_28_out, and_29_out, and_30_out);
endmodule

module \Шифратор_дешифратор  (
  input  [9:0] in_1,
  output [7:0] out_2,
  output out_3
);

  wire [3:0] \шифратор_0_9_в1_1_out_11 ;

  \Шифратор_0_9_В1  \u_шифратор_0_9_в1_1  (
    .x9(in_1[9]), .x8(in_1[8]), .x7(in_1[7]), .x6(in_1[6]), .x5(in_1[5]), .x4(in_1[4]), .x3(in_1[3]),
    .x2(in_1[2]), .x1(in_1[1]), .x0(in_1[0]), .out_11(\шифратор_0_9_в1_1_out_11 ), .M(out_3));
  \Дешифратор_0_9  \u_дешифратор_0_9_1  (
    .x3(\шифратор_0_9_в1_1_out_11 [3]), .x2(\шифратор_0_9_в1_1_out_11 [2]),
    .x1(\шифратор_0_9_в1_1_out_11 [1]), .x0(\шифратор_0_9_в1_1_out_11 [0]), .y7(out_2[7]), .y6(out_2[6]),
    .y5(out_2[5]), .y4(out_2[4]), .y3(out_2[3]), .y2(out_2[2]), .y1(out_2[1]), .y0(out_2[0]));  // open: M
  _7_Segment_Display u_7_segment_display_1 (
    .g(out_2[3]), .f(out_2[2]), .a(out_2[1]), .b(out_2[0]), .e(out_2[4]), .d(out_2[5]), .c(out_2[6]),
    .dp(out_2[7]));

  // Notes on the sheet:
  //   На вход идут числа справа на лево
  //   При первой 1, всех нулях и неправильных числах на выводе будет ноль
  //   Неправильное число
endmodule

module MUX (
  input  x0,
  input  x1,
  input  x2,
  input  x3,
  input  x4,
  input  x5,
  input  x6,
  input  x7,
  input  m0,
  input  m1,
  input  m2,
  output out_12
);

  wire and_1_out, and_2_out, and_3_out, and_4_out, and_5_out, and_6_out, and_7_out, and_8_out, not_1_out,
       not_2_out, not_3_out;

  not not_1 (not_1_out, m0);
  not not_2 (not_2_out, m1);
  not not_3 (not_3_out, m2);
  and and_1 (and_1_out, x0, not_1_out, not_2_out, not_3_out);
  and and_2 (and_2_out, x1, not_1_out, not_2_out, m2);
  and and_3 (and_3_out, x2, not_1_out, not_3_out, m1);
  and and_4 (and_4_out, x3, not_1_out, m1, m2);
  and and_5 (and_5_out, x4, m0, not_2_out, not_3_out);
  and and_6 (and_6_out, x5, m0, not_2_out, m2);
  and and_7 (and_7_out, x6, m0, m1, not_3_out);
  and and_8 (and_8_out, x7, m0, m1, m2);
  or or_1 (out_12, and_1_out, and_2_out, and_3_out, and_4_out, and_5_out, and_6_out, and_7_out, and_8_out);
endmodule

module DEMUX (
  input  I,
  input  m0,
  input  m1,
  output out_4,
  output out_5,
  output out_6,
  output out_7
);

  wire not_1_out, not_2_out;

  not not_1 (not_1_out, m1);
  not not_2 (not_2_out, m0);
  and and_1 (out_4, I, not_2_out, not_1_out);
  and and_2 (out_5, I, m0, not_1_out);
  and and_3 (out_6, I, not_2_out, m1);
  and and_4 (out_7, I, m0, m1);
endmodule
