// Logisim project Счетчик.circ as structural Verilog: 2 circuits, main circuit Счетчик
module \Счетчик  (
  input  en,
  input  _0,
  input  [3:0] in_3,
  input  in_4,
  output [3:0] out_5
);

  wire and_1_out, and_2_out, and_3_out, and_4_out, clock_1_out, d_ff_1_qn, d_ff_2_qn, d_ff_3_qn, d_ff_4_qn;

  Clock clock_1 (.out(clock_1_out));
  and and_1 (and_1_out, in_3[0], clock_1_out, in_4);
  and and_2 (and_2_out, in_3[1], clock_1_out, in_4);
  and and_3 (and_3_out, in_3[2], clock_1_out, in_4);
  and and_4 (and_4_out, in_3[3], clock_1_out, in_4);
  D_Flip_Flop d_ff_1 (
    .clk(clock_1_out), .D(d_ff_1_qn), .Q(out_5[0]), .Qn(d_ff_1_qn), .preset(and_1_out), .en(en), .reset(_0));
  D_Flip_Flop d_ff_2 (
    .clk(d_ff_1_qn), .D(d_ff_2_qn), .Q(out_5[1]), .Qn(d_ff_2_qn), .preset(and_2_out), .en(en), .reset(_0));
  D_Flip_Flop d_ff_3 (
    .clk(d_ff_2_qn), .D(d_ff_3_qn), .Q(out_5[2]), .Qn(d_ff_3_qn), .preset(and_3_out), .en(en), .reset(_0));
  D_Flip_Flop d_ff_4 (
    .clk(d_ff_3_qn), .D(d_ff_4_qn), .Q(out_5[3]), .Qn(d_ff_4_qn), .preset(and_4_out), .en(en), .reset(_0));
  // Probe on out_5
endmodule

module \Регистр  (
  input  [7:0] in_1,
  input  Ena,
  input  Clr,
  output [7:0] out_4
);

  wire clock_1_out;

  Clock clock_1 (.out(clock_1_out));
  D_Flip_Flop d_ff_1 (.clk(clock_1_out), .D(in_1[0]), .Q(out_4[0]), .en(Ena), .reset(Clr));  // open: Qn, preset
  D_Flip_Flop d_ff_2 (.clk(clock_1_out), .D(in_1[1]), .Q(out_4[1]), .en(Ena), .reset(Clr));  // open: Qn, preset
  D_Flip_Flop d_ff_3 (.clk(clock_1_out), .D(in_1[2]), .Q(out_4[2]), .en(Ena), .reset(Clr));  // open: Qn, preset
  D_Flip_Flop d_ff_4 (.clk(clock_1_out), .D(in_1[3]), .Q(out_4[3]), .en(Ena), .reset(Clr));  // open: Qn, preset
  D_Flip_Flop d_ff_5 (.clk(clock_1_out), .D(in_1[4]), .Q(out_4[4]), .en(Ena), .reset(Clr));  // open: Qn, preset
  D_Flip_Flop d_ff_6 (.clk(clock_1_out), .D(in_1[5]), .Q(out_4[5]), .en(Ena), .reset(Clr));  // open: Qn, preset
  D_Flip_Flop d_ff_7 (.clk(clock_1_out), .D(in_1[6]), .Q(out_4[6]), .en(Ena), .reset(Clr));  // open: Qn, preset
  D_Flip_Flop d_ff_8 (.clk(clock_1_out), .D(in_1[7]), .Q(out_4[7]), .en(Ena), .reset(Clr));  // open: Qn, preset
endmodule
