// Logisim project Сумматор, Вычитатор, умножатор — копия.circ as structural Verilog: 10 circuits, main circuit Полусумматор
module \Полусумматор  (
  input  A,
  input  B,
  output SUM,
  output CARRY
);

  xor xor_1 (SUM, A, B);
  and and_1 (CARRY, A, B);
endmodule

module \Сумматор  (
  input  CI,
  input  A,
  input  B,
  output out_4,
  output out_5
);

  wire \полусумматор_1_carry , \полусумматор_1_sum , \полусумматор_2_carry ;

  \Полусумматор  \u_полусумматор_1  (.A(A), .B(B), .SUM(\полусумматор_1_sum ), .CARRY(\полусумматор_1_carry ));
  \Полусумматор  \u_полусумматор_2  (.A(CI), .B(\полусумматор_1_sum ), .SUM(out_4), .CARRY(\полусумматор_2_carry ));
  or or_1 (out_5, \полусумматор_2_carry , \полусумматор_1_carry );
endmodule

module \Сумматор_4бит  (
  input  [3:0] A,
  input  [3:0] B,
  output out_3,
  output [3:0] out_4
);

  wire \сумматор_2_out_5 , \сумматор_3_out_5 , \сумматор_4_out_5 ;

  // Probe on A
  // Probe on B
  \Сумматор  \u_сумматор_1  (.CI(A[3]), .A(B[3]), .B(\сумматор_2_out_5 ), .out_4(out_4[3]), .out_5(out_3));
  \Сумматор  \u_сумматор_2  (.CI(A[2]), .A(B[2]), .B(\сумматор_3_out_5 ), .out_4(out_4[2]), .out_5(\сумматор_2_out_5 ));
  \Сумматор  \u_сумматор_3  (.CI(A[1]), .A(B[1]), .B(\сумматор_4_out_5 ), .out_4(out_4[1]), .out_5(\сумматор_3_out_5 ));
  \Сумматор  \u_сумматор_4  (.CI(A[0]), .A(B[0]), .B(1'b0), .out_4(out_4[0]), .out_5(\сумматор_4_out_5 ));
endmodule

module \Сумматор_8бит  (
  input  [7:0] A,
  input  [7:0] B,
  input  \Вычитание ,
  output out_4,
  output [7:0] out_5
);

  wire \сумматор_2_out_5 , \сумматор_3_out_5 , \сумматор_4_out_5 , \сумматор_5_out_5 , \сумматор_6_out_5 ,
       \сумматор_7_out_5 , \сумматор_8_out_5 ;
  wire [7:0] \инвертор_1_out_3 ;

  // Probe on A
  // Probe on \инвертор_1_out_3 
  \Инвертор  \u_инвертор_1  (.in_1(B), .in_2(\Вычитание ), .out_3(\инвертор_1_out_3 ));
  // Probe on out_5
  \Сумматор  \u_сумматор_1  (
    .CI(A[7]), .A(\инвертор_1_out_3 [7]), .B(\сумматор_2_out_5 ), .out_4(out_5[7]), .out_5(out_4));
  \Сумматор  \u_сумматор_2  (
    .CI(A[6]), .A(\инвертор_1_out_3 [6]), .B(\сумматор_3_out_5 ), .out_4(out_5[6]), .out_5(\сумматор_2_out_5 ));
  \Сумматор  \u_сумматор_3  (
    .CI(A[5]), .A(\инвертор_1_out_3 [5]), .B(\сумматор_4_out_5 ), .out_4(out_5[5]), .out_5(\сумматор_3_out_5 ));
  \Сумматор  \u_сумматор_4  (
    .CI(A[4]), .A(\инвертор_1_out_3 [4]), .B(\сумматор_5_out_5 ), .out_4(out_5[4]), .out_5(\сумматор_4_out_5 ));
  \Сумматор  \u_сумматор_5  (
    .CI(A[3]), .A(\инвертор_1_out_3 [3]), .B(\сумматор_6_out_5 ), .out_4(out_5[3]), .out_5(\сумматор_5_out_5 ));
  \Сумматор  \u_сумматор_6  (
    .CI(A[2]), .A(\инвертор_1_out_3 [2]), .B(\сумматор_7_out_5 ), .out_4(out_5[2]), .out_5(\сумматор_6_out_5 ));
  \Сумматор  \u_сумматор_7  (
    .CI(A[1]), .A(\инвертор_1_out_3 [1]), .B(\сумматор_8_out_5 ), .out_4(out_5[1]), .out_5(\сумматор_7_out_5 ));
  \Сумматор  \u_сумматор_8  (
    .CI(A[0]), .A(\инвертор_1_out_3 [0]), .B(\Вычитание ), .out_4(out_5[0]), .out_5(\сумматор_8_out_5 ));
endmodule

module \Вычитатор_4бит__бета  (
  input  [3:0] B,
  input  [3:0] \Константная_1 ,
  input  [3:0] A,
  output [3:0] out_4,
  output [3:0] \Разность 
);

  wire not_1_out, not_2_out, not_3_out, not_4_out, \сумматор_3_out_5 , \сумматор_4_out_5 ,
       \сумматор_5_out_5 , \сумматор_6_out_5 , \сумматор_7_out_5 , \сумматор_8_out_5 ;

  // Probe on B
  // Probe on \Разность 
  not not_1 (not_1_out, B[0]);
  not not_2 (not_2_out, B[1]);
  not not_3 (not_3_out, B[2]);
  not not_4 (not_4_out, B[3]);
  // Probe on \Константная_1 
  // Probe on A
  \Сумматор  \u_сумматор_1  (
    .CI(not_4_out), .A(\Константная_1 [3]), .B(\сумматор_3_out_5 ), .out_4(out_4[3]));  // open: out_5
  \Сумматор  \u_сумматор_2  (.CI(A[3]), .A(out_4[3]), .B(\сумматор_4_out_5 ), .out_4(\Разность [3]));  // open: out_5
  \Сумматор  \u_сумматор_3  (
    .CI(not_3_out), .A(\Константная_1 [2]), .B(\сумматор_5_out_5 ), .out_4(out_4[2]),
    .out_5(\сумматор_3_out_5 ));
  \Сумматор  \u_сумматор_4  (
    .CI(A[2]), .A(out_4[2]), .B(\сумматор_6_out_5 ), .out_4(\Разность [2]), .out_5(\сумматор_4_out_5 ));
  \Сумматор  \u_сумматор_5  (
    .CI(not_2_out), .A(\Константная_1 [1]), .B(\сумматор_7_out_5 ), .out_4(out_4[1]),
    .out_5(\сумматор_5_out_5 ));
  \Сумматор  \u_сумматор_6  (
    .CI(A[1]), .A(out_4[1]), .B(\сумматор_8_out_5 ), .out_4(\Разность [1]), .out_5(\сумматор_6_out_5 ));
  \Сумматор  \u_сумматор_7  (
    .CI(not_1_out), .A(\Константная_1 [0]), .B(1'b0), .out_4(out_4[0]), .out_5(\сумматор_7_out_5 ));
  \Сумматор  \u_сумматор_8  (.CI(A[0]), .A(out_4[0]), .B(1'b0), .out_4(\Разность [0]), .out_5(\сумматор_8_out_5 ));

  // Notes on the sheet:
  //   Прибавляем к нему 1
  //   Инвертируем число при помощи ф-ции НЕ
  //   сложение положительного и отрицательного числа
  //   Вывод полученного отрицательного числа (для проверки)
endmodule

module \Инвертор  (
  input  [7:0] in_1,
  input  in_2,
  output [7:0] out_3
);

  xor xor_1 (out_3[7], in_2, in_1[7]);
  xor xor_2 (out_3[6], in_2, in_1[6]);
  xor xor_3 (out_3[5], in_2, in_1[5]);
  xor xor_4 (out_3[4], in_2, in_1[4]);
  xor xor_5 (out_3[3], in_2, in_1[3]);
  xor xor_6 (out_3[2], in_2, in_1[2]);
  xor xor_7 (out_3[0], in_2, in_1[0]);
  xor xor_8 (out_3[1], in_2, in_1[1]);
endmodule

module \Вычитатор  (
  input  [7:0] in_1,
  input  [7:0] in_2,
  input  in_3,
  output out_4,
  output [7:0] out_5
);

  wire \сумматор_8бит_1_p1 ;
  wire [7:0] \инвертор_1_out_3 ;

  // Probe on in_1
  // Probe on in_2
  // Probe on in_2
  // Probe on in_1
  xor xor_1 (out_4, in_3, \сумматор_8бит_1_p1 );
  \Инвертор  \u_инвертор_1  (.in_1(in_2), .in_2(in_3), .out_3(\инвертор_1_out_3 ));
  // Probe on out_5
  // Probe on out_5
  // Сумматор_8бит сумматор_8бит_1: pin names not known; wires that end beside it: \сумматор_8бит_1_p1 , in_1, out_5, \инвертор_1_out_3 , in_3

  // Notes on the sheet:
  //   A
  //   B
  //   A
  //   B
endmodule

module \Умножатор  (
  input  [3:0] A,
  input  [3:0] B,
  output [7:0] out_3
);

  wire and_1_out, and_2_out, and_3_out, and_4_out, and_5_out, and_6_out, and_7_out, and_8_out, and_9_out,
       and_10_out, and_11_out, and_12_out, and_13_out, and_14_out, and_15_out, \сумматор_2_out_4 ,
       \сумматор_2_out_5 , \сумматор_3_out_4 , \сумматор_3_out_5 , \сумматор_4_out_4 , \сумматор_4_out_5 ,
       \сумматор_5_out_5 , \сумматор_6_out_4 , \сумматор_6_out_5 , \сумматор_7_out_5 , \сумматор_8_out_4 ,
       \сумматор_8_out_5 , \сумматор_9_out_4 , \сумматор_9_out_5 , \сумматор_10_out_5 , \сумматор_11_out_5 ,
       \сумматор_12_out_5 ;

  // Probe on out_3
  and and_1 (and_1_out, A[3], B[3]);
  \Сумматор  \u_сумматор_1  (
    .CI(\сумматор_3_out_5 ), .A(and_1_out), .B(\сумматор_5_out_5 ), .out_4(out_3[6]), .out_5(out_3[7]));
  and and_2 (and_2_out, A[3], B[1]);
  \Сумматор  \u_сумматор_2  (
    .CI(1'b0), .A(and_2_out), .B(\сумматор_6_out_5 ), .out_4(\сумматор_2_out_4 ), .out_5(\сумматор_2_out_5 ));
  and and_3 (and_3_out, A[3], B[2]);
  \Сумматор  \u_сумматор_3  (
    .CI(\сумматор_2_out_5 ), .A(and_3_out), .B(\сумматор_4_out_5 ), .out_4(\сумматор_3_out_4 ),
    .out_5(\сумматор_3_out_5 ));
  and and_4 (and_4_out, A[2], B[3]);
  and and_5 (and_5_out, A[2], B[1]);
  and and_6 (and_6_out, A[2], B[2]);
  \Сумматор  \u_сумматор_4  (
    .CI(\сумматор_2_out_4 ), .A(and_6_out), .B(\сумматор_9_out_5 ), .out_4(\сумматор_4_out_4 ),
    .out_5(\сумматор_4_out_5 ));
  and and_7 (and_7_out, A[1], B[3]);
  \Сумматор  \u_сумматор_5  (
    .CI(\сумматор_3_out_4 ), .A(and_4_out), .B(\сумматор_7_out_5 ), .out_4(out_3[5]),
    .out_5(\сумматор_5_out_5 ));
  and and_8 (and_8_out, A[3], B[0]);
  \Сумматор  \u_сумматор_6  (
    .CI(and_8_out), .A(and_5_out), .B(\сумматор_8_out_5 ), .out_4(\сумматор_6_out_4 ),
    .out_5(\сумматор_6_out_5 ));
  and and_9 (and_9_out, A[1], B[2]);
  \Сумматор  \u_сумматор_7  (
    .CI(\сумматор_4_out_4 ), .A(and_7_out), .B(\сумматор_10_out_5 ), .out_4(out_3[4]),
    .out_5(\сумматор_7_out_5 ));
  and and_10 (and_10_out, A[2], B[0]);
  and and_11 (and_11_out, A[1], B[1]);
  \Сумматор  \u_сумматор_8  (
    .CI(and_10_out), .A(and_11_out), .B(\сумматор_11_out_5 ), .out_4(\сумматор_8_out_4 ),
    .out_5(\сумматор_8_out_5 ));
  \Сумматор  \u_сумматор_9  (
    .CI(\сумматор_6_out_4 ), .A(and_9_out), .B(\сумматор_12_out_5 ), .out_4(\сумматор_9_out_4 ),
    .out_5(\сумматор_9_out_5 ));
  and and_12 (and_12_out, A[0], B[3]);
  \Сумматор  \u_сумматор_10  (
    .CI(\сумматор_9_out_4 ), .A(and_12_out), .B(1'b0), .out_4(out_3[3]), .out_5(\сумматор_10_out_5 ));
  and and_13 (and_13_out, A[1], B[0]);
  and and_14 (and_14_out, A[0], B[1]);
  \Сумматор  \u_сумматор_11  (.CI(and_13_out), .A(and_14_out), .B(1'b0), .out_4(out_3[1]), .out_5(\сумматор_11_out_5 ));
  and and_15 (and_15_out, A[0], B[2]);
  \Сумматор  \u_сумматор_12  (
    .CI(\сумматор_8_out_4 ), .A(and_15_out), .B(1'b0), .out_4(out_3[2]), .out_5(\сумматор_12_out_5 ));
  and and_16 (out_3[0], A[0], B[0]);
  // Probe on A
  // Probe on B

  // Notes on the sheet:
  //   а4
  //   а4
  //   а4
  //   а3
  //   а3
  //   а4
  //   а3
  //   а2
  //   а3
  //   а2
  //   а2
  //   а1
  //   а1
  //   а1
  //   а2
  //   а1
  //   *
endmodule

module \Сумматор_с_памятью  (
  input  [7:0] A,
  input  [7:0] B,
  input  \Вычитание ,
  input  \Из_памяти ,
  input  \Запись_в_память ,
  input  \Очистить ,
  output [7:0] out_7,
  output out_8
);

  wire [7:0] multiplexer_1_out, \регистр_1_out_5 ;

  // Probe on A
  // Probe on B
  // Probe on \регистр_1_out_5 
  Multiplexer #(.width(8)) multiplexer_1 (
    .in0(B), .in1(\регистр_1_out_5 ), .out(multiplexer_1_out), .sel(\Из_памяти ));  // open: en
  \Сумматор_8бит  \u_сумматор_8бит_1  (
    .A(A), .B(multiplexer_1_out), .out_5(out_7), .out_4(out_8), .\Вычитание (\Вычитание ));
  \регистр  \u_регистр_1  (
    .in_1(\Запись_в_память ), .in_2(out_7), .Ena(\Запись_в_память ), .Clr(\Очистить ),
    .out_5(\регистр_1_out_5 ));
  // Probe on out_7
endmodule

module \регистр  (
  input  in_1,
  input  [7:0] in_2,
  input  Ena,
  input  Clr,
  output [7:0] out_5
);

  D_Flip_Flop d_ff_1 (.clk(in_1), .D(in_2[0]), .Q(out_5[0]), .en(Ena), .reset(Clr));  // open: Qn, preset
  D_Flip_Flop d_ff_2 (.clk(in_1), .D(in_2[1]), .Q(out_5[1]), .en(Ena), .reset(Clr));  // open: Qn, preset
  D_Flip_Flop d_ff_3 (.clk(in_1), .D(in_2[2]), .Q(out_5[2]), .en(Ena), .reset(Clr));  // open: Qn, preset
  D_Flip_Flop d_ff_4 (.clk(in_1), .D(in_2[3]), .Q(out_5[3]), .en(Ena), .reset(Clr));  // open: Qn, preset
  D_Flip_Flop d_ff_5 (.clk(in_1), .D(in_2[4]), .Q(out_5[4]), .en(Ena), .reset(Clr));  // open: Qn, preset
  D_Flip_Flop d_ff_6 (.clk(in_1), .D(in_2[5]), .Q(out_5[5]), .en(Ena), .reset(Clr));  // open: Qn, preset
  D_Flip_Flop d_ff_7 (.clk(in_1), .D(in_2[6]), .Q(out_5[6]), .en(Ena), .reset(Clr));  // open: Qn, preset
  D_Flip_Flop d_ff_8 (.clk(in_1), .D(in_2[7]), .Q(out_5[7]), .en(Ena), .reset(Clr));  // open: Qn, preset
endmodule
